// Digital circuit Ejemplos bancos de Memorias.dig as structural Verilog
module Ejemplos_bancos_de_Memorias (
  input  [13:0] in_1,
  input  in_2,
  input  in_3,
  input  [1:0] in_4,
  input  [7:0] in_5,
  input  [18:0] in_6,
  input  in_7,
  input  in_8,
  input  [1:0] in_9,
  input  [7:0] in_10,
  input  [7:0] in_11
);

  wire decoder_1_out_0, decoder_1_out_1, decoder_1_out_2, decoder_1_out_3, decoder_2_out_0, decoder_2_out_1,
       decoder_2_out_2, decoder_2_out_3;

  Decoder #(.Selector_Bits(2)) decoder_1 (
    .sel(in_4), .out_0(decoder_1_out_0), .out_1(decoder_1_out_1), .out_2(decoder_1_out_2),
    .out_3(decoder_1_out_3));
  RAMSinglePortSel #(.AddrBits(14), .Bits(8)) ramsingleportsel_1 (
    .A(in_1), .CS(decoder_1_out_3), .WE(in_3), .OE(in_2), .D(in_5));
  RAMSinglePortSel #(.AddrBits(14), .Bits(8)) ramsingleportsel_2 (
    .A(in_1), .CS(decoder_1_out_2), .WE(in_3), .OE(in_2), .D(in_5));
  RAMSinglePortSel #(.AddrBits(14), .Bits(8)) ramsingleportsel_3 (
    .A(in_1), .CS(decoder_1_out_1), .WE(in_3), .OE(in_2), .D(in_5));
  RAMSinglePortSel #(.AddrBits(14), .Bits(8)) ramsingleportsel_4 (
    .A(in_1), .CS(decoder_1_out_0), .WE(in_3), .OE(in_2), .D(in_5));
  Decoder #(.Selector_Bits(2)) decoder_2 (
    .sel(in_9), .out_0(decoder_2_out_0), .out_1(decoder_2_out_1), .out_2(decoder_2_out_2),
    .out_3(decoder_2_out_3));
  RAMSinglePortSel #(.AddrBits(19), .Bits(8)) ramsingleportsel_5 (
    .A(in_6), .CS(decoder_2_out_3), .WE(in_8), .OE(in_7), .D(in_10));
  RAMSinglePortSel #(.AddrBits(19), .Bits(8)) ramsingleportsel_6 (
    .A(in_6), .CS(decoder_2_out_3), .WE(in_8), .OE(in_7), .D(in_11));
  RAMSinglePortSel #(.AddrBits(19), .Bits(8)) ramsingleportsel_7 (
    .A(in_6), .CS(decoder_2_out_2), .WE(in_8), .OE(in_7), .D(in_10));
  RAMSinglePortSel #(.AddrBits(19), .Bits(8)) ramsingleportsel_8 (
    .A(in_6), .CS(decoder_2_out_2), .WE(in_8), .OE(in_7), .D(in_11));
  RAMSinglePortSel #(.AddrBits(19), .Bits(8)) ramsingleportsel_9 (
    .A(in_6), .CS(decoder_2_out_1), .WE(in_8), .OE(in_7), .D(in_10));
  RAMSinglePortSel #(.AddrBits(19), .Bits(8)) ramsingleportsel_10 (
    .A(in_6), .CS(decoder_2_out_1), .WE(in_8), .OE(in_7), .D(in_11));
  RAMSinglePortSel #(.AddrBits(19), .Bits(8)) ramsingleportsel_11 (
    .A(in_6), .CS(decoder_2_out_0), .WE(in_8), .OE(in_7), .D(in_10));
  RAMSinglePortSel #(.AddrBits(19), .Bits(8)) ramsingleportsel_12 (
    .A(in_6), .CS(decoder_2_out_0), .WE(in_8), .OE(in_7), .D(in_11));

  // Notes on the sheet:
  //   A15-A14
  //   A13-A0
  //   Escritura
  //   Lectura
  //   D7-D0
  //   64K x 8 con chips de 16K x 8
  //   49152
  //   65535
  //   Direcciones
  //   32768
  //   49151
  //   16384
  //   32767
  //   0
  //   16383
  //   A21-A20
  //   A19-A0
  //   D15-D8
  //   4M x 16 con chips de 1M x 8
endmodule
